# Fritzing sketch Motherboard (saved by Fritzing 0.9.3b)
circuit board: 12.5401cm x 16.0699cm
breadboards: 1

parts:
  Op_Amp = IC, DIP package, 8 pins [chip_label=IC]
  Op_Amp_2 = IC, DIP package, 8 pins [chip_label=IC]
  Converter = IC, DIP package, 8 pins [chip_label=IC]
  4_7K2 = Resistor [tolerance=±5% resistance=4.7k package=THT]
  4_7K3 = Resistor [tolerance=±5% resistance=4.7k package=THT]
  4_7K4 = Resistor [tolerance=±5% resistance=4.7k package=THT]
  C2 = Electrolytic Capacitor [capacitance=100µF package="100 mil [THT, electrolytic]"]
  Arduino_Mega1 = Arduino Mega 2560 (Rev3)
  Driver_1 = screw terminal, 2 pins
  10u8 = Ceramic Capacitor [capacitance=10µF package="200 mil [THT, multilayer]"]
  10u = Ceramic Capacitor [capacitance=10µF package="200 mil [THT, multilayer]"]
  10u7 = Ceramic Capacitor [capacitance=10µF package="200 mil [THT, multilayer]"]
  10u6 = Ceramic Capacitor [capacitance=10µF package="200 mil [THT, multilayer]"]
  10u5 = Ceramic Capacitor [capacitance=10µF package="200 mil [THT, multilayer]"]
  Op_Amp_3 = IC, DIP package, 8 pins [chip_label=IC]
  10u12 = Ceramic Capacitor [capacitance=10µF package="200 mil [THT, multilayer]"]
  10u13 = Ceramic Capacitor [capacitance=10µF package="200 mil [THT, multilayer]"]
  4_7K5 = Resistor [tolerance=±5% resistance=4.7k package=THT]
  47K = Resistor [tolerance=±5% resistance=47k package=THT]
  4_7K7 = Resistor [tolerance=±5% resistance=4.7k package=THT]
  C3 = Electrolytic Capacitor [capacitance=100µF package="100 mil [THT, electrolytic]"]
  Detector = screw terminal, 2 pins
  Driver_2 = screw terminal, 2 pins
  R2 = Resistor [tolerance=±5% resistance=4.7k package=THT]
  J414 = female pin header, 2 pins [form="♀ (female)"]
  J415 = female pin header, 6 pins [form="♀ (female)"]
  Fans = screw terminal, 4 pins
  GND = female pin header, 1 pin [form="♀ (female)"]
  5V = female pin header, 1 pin [form="♀ (female)"]
  12V = female pin header, 1 pin [form="♀ (female)"]
  J472 = female pin header, 1 pin [form="♀ (female)"]
  J473 = female pin header, 1 pin [form="♀ (female)"]
  J474 = female pin header, 1 pin [form="♀ (female)"]  # not connected
  J475 = female pin header, 1 pin [form="♀ (female)"]
  J476 = female pin header, 1 pin [form="♀ (female)"]
  J477 = female pin header, 1 pin [form="♀ (female)"]
  J478 = female pin header, 1 pin [form="♀ (female)"]
  390 = Resistor [tolerance=±5% resistance=390 package=THT]
  NPN = NPN-Transistor [package="TO92 [THT]"]
  100 = Resistor [tolerance=±5% resistance=390 package=THT]
  1M = Resistor [tolerance=±5% resistance=390 package=THT]
  P-ch = NPN-Transistor [package="TO92 [THT]"]
  390_2 = Resistor [tolerance=±5% resistance=390 package=THT]
  NPN_2 = NPN-Transistor [package="TO92 [THT]"]
  390_3 = Resistor [tolerance=±5% resistance=390 package=THT]
  NPN_3 = NPN-Transistor [package="TO92 [THT]"]
  390_4 = Resistor [tolerance=±5% resistance=390 package=THT]
  390_5 = Resistor [tolerance=±5% resistance=390 package=THT]
  NPN_4 = NPN-Transistor [package="TO92 [THT]"]
  NPN_5 = NPN-Transistor [package="TO92 [THT]"]
  -_Diode_+8 = Diode [package=diode-1n4148]
  -_Diode_+9 = Diode [package=diode-1n4148]
  J509 = female pin header, 1 pin [form="♀ (female)"]
  J510 = female pin header, 1 pin [form="♀ (female)"]
  J511 = female pin header, 1 pin [form="♀ (female)"]
  J513 = female pin header, 1 pin [form="♀ (female)"]  # not connected
  J514 = female pin header, 1 pin [form="♀ (female)"]  # not connected
  J516 = female pin header, 1 pin [form="♀ (female)"]  # not connected
  J517 = female pin header, 1 pin [form="♀ (female)"]  # not connected
  J518 = female pin header, 1 pin [form="♀ (female)"]
  J519 = female pin header, 1 pin [form="♀ (female)"]
  J520 = female pin header, 1 pin [form="♀ (female)"]
  J521 = female pin header, 1 pin [form="♀ (female)"]
  J523 = female pin header, 1 pin [form="♀ (female)"]
  J524 = female pin header, 1 pin [form="♀ (female)"]
  J525 = female pin header, 1 pin [form="♀ (female)"]
  J528 = female pin header, 1 pin [form="♀ (female)"]
  J529 = female pin header, 1 pin [form="♀ (female)"]  # not connected
  J530 = female pin header, 1 pin [form="♀ (female)"]
  J527 = female pin header, 1 pin [form="♀ (female)"]
  J526 = female pin header, 1 pin [form="♀ (female)"]
  J531 = female pin header, 1 pin [form="♀ (female)"]
  J532 = female pin header, 1 pin [form="♀ (female)"]
  J533 = female pin header, 1 pin [form="♀ (female)"]
  J534 = female pin header, 1 pin [form="♀ (female)"]  # not connected
  J535 = female pin header, 1 pin [form="♀ (female)"]
  J537 = female pin header, 1 pin [form="♀ (female)"]
  J538 = female pin header, 1 pin [form="♀ (female)"]
  J539 = female pin header, 1 pin [form="♀ (female)"]
  J540 = female pin header, 1 pin [form="♀ (female)"]
  J541 = female pin header, 1 pin [form="♀ (female)"]  # not connected
  J542 = female pin header, 1 pin [form="♀ (female)"]
  J543 = female pin header, 1 pin [form="♀ (female)"]
  J544 = female pin header, 1 pin [form="♀ (female)"]  # not connected
  -_Diode_+10 = Diode [package=diode-1n4148]
  NPN_6 = NPN-Transistor [package="TO92 [THT]"]
  390_6 = Resistor [tolerance=±5% resistance=390 package=THT]
  -_Diode_+11 = Diode [package=diode-1n4148]
  NPN_7 = NPN-Transistor [package="TO92 [THT]"]
  390_7 = Resistor [tolerance=±5% resistance=390 package=THT]

nets:
  N1: Op_Amp.pin1, Op_Amp.pin2, 4_7K4.Pin_0
  N2: Op_Amp.pin3, 4_7K3.Pin_1, 10u8.1
  N3: Op_Amp.pin4, Op_Amp_2.pin4, Converter.pin3, C2.+, Arduino_Mega1.GND, Driver_1.pin2, 10u8.0, 10u.0, 10u6.1, 10u5.1, Op_Amp_3.pin4, 10u12.1, 10u13.0, 47K.Pin_1, C3.+, Detector.pin2, Driver_2.pin2, J415.pin4, Fans.pin2, Fans.pin4, GND.pin1, J473.pin1, J477.pin1, NPN.E, NPN_2.E, NPN_3.E, NPN_4.E, NPN_5.E, J524.pin1, J528.pin1, J535.pin1, J543.pin1, NPN_6.E, NPN_7.E
  N4: Op_Amp.pin5, 4_7K4.Pin_1, Arduino_Mega1.A0, 10u.1
  N5: Op_Amp.pin6, Op_Amp.pin7, Driver_1.pin1
  N6: Op_Amp.pin8, Op_Amp_2.pin8, Converter.pin8, Arduino_Mega1.5V, 10u5.0, Op_Amp_3.pin8, J475.pin1, J526.pin1
  N7: Op_Amp_2.pin1, Op_Amp_2.pin2, Arduino_Mega1.A5, J472.pin1
  N8: Op_Amp_2.pin3, C3.-, R2.Pin_1
  N9: Op_Amp_2.pin5, 4_7K2.Pin_1, C2.-
  N10: Op_Amp_2.pin6, Op_Amp_2.pin7, Arduino_Mega1.A2, J527.pin1
  N11: Converter.pin2, 10u7.0
  N12: Converter.pin4, 10u7.1
  N13: Converter.pin5, 10u6.0, J476.pin1, J530.pin1
  N14: 4_7K2.Pin_0, Arduino_Mega1.D11_PWM
  N15: 4_7K3.Pin_0, Arduino_Mega1.D12_PWM
  N16: Arduino_Mega1.A9, J478.pin1
  N17: Arduino_Mega1.A12, J519.pin1
  N18: Arduino_Mega1.A13, J539.pin1
  N19: Arduino_Mega1.A14, J520.pin1
  N20: Arduino_Mega1.A15, J537.pin1
  N21: Arduino_Mega1.A3, J525.pin1
  N22: Arduino_Mega1.A6, 47K.Pin_0, Detector.pin1
  N23: Arduino_Mega1.A7, Op_Amp_3.pin5, 10u12.0, 4_7K5.Pin_1
  N24: Arduino_Mega1.D21/SCL, 390_4.Pin_1
  N25: Arduino_Mega1.D19/RX1, 390_3.Pin_1
  N26: Arduino_Mega1.D17_PWM/RX2, 390_2.Pin_1
  N27: Arduino_Mega1.D14/TX3, 100.Pin_0, 1M.Pin_0
  N28: Arduino_Mega1.D9_PWM, R2.Pin_0
  N29: Arduino_Mega1.D8_PWM, 4_7K7.Pin_0
  N30: Arduino_Mega1.D3_PWM, J415.pin3
  N31: Arduino_Mega1.D4_PWM, J415.pin2
  N32: Arduino_Mega1.D5_PWM, J415.pin1
  N33: Arduino_Mega1.D47, 390_5.Pin_1
  N34: Arduino_Mega1.D49, 390_6.Pin_1
  N35: Arduino_Mega1.D51, 390_7.Pin_1
  N36: Arduino_Mega1.D53, 390.Pin_1
  N37: Op_Amp_3.pin1, Op_Amp_3.pin2, 4_7K5.Pin_0
  N38: Op_Amp_3.pin3, 10u13.1, 4_7K7.Pin_1
  N39: Op_Amp_3.pin6, Op_Amp_3.pin7, Driver_2.pin1
  N40: J414.pin1, J533.pin1
  N41: J414.pin2, J531.pin1
  N42: J415.pin6, 5V.pin1, 1M.Pin_1, P-ch.E
  N43: Fans.pin1, Fans.pin3, 12V.pin1, -_Diode_+8.C, -_Diode_+9.C, J532.pin1, J538.pin1, -_Diode_+10.C, -_Diode_+11.C
  N44: 390.Pin_0, NPN.B
  N45: NPN.C, -_Diode_+8.A, J521.pin1
  N46: 100.Pin_1, P-ch.B
  N47: P-ch.C, J509.pin1
  N48: 390_2.Pin_0, NPN_2.B
  N49: NPN_2.C, J510.pin1
  N50: 390_3.Pin_0, NPN_3.B
  N51: NPN_3.C, J518.pin1
  N52: 390_4.Pin_0, NPN_5.B
  N53: 390_5.Pin_0, NPN_4.B
  N54: NPN_4.C, J540.pin1, -_Diode_+10.A
  N55: NPN_5.C, J523.pin1
  N56: -_Diode_+9.A, J511.pin1, NPN_6.C
  N57: J542.pin1, -_Diode_+11.A, NPN_7.C
  N58: NPN_6.B, 390_6.Pin_0
  N59: NPN_7.B, 390_7.Pin_0

notes:
  GND
  Blk
  Thk
  R
  G
  W
  B
  Thick
  Black
  Thick GND
  Voltage
  Red
  Two Colour
  12V
  Sensor 2
  Sensor 1
